// Digital circuit 17008425.dig as structural Verilog
module _17008425 (
  input  B0,
  input  B1,
  input  B2,
  input  B3,
  input  B4,
  input  B5,
  input  B6,
  input  B7,
  input  B8,
  input  B9,
  input  CLK,
  input  Parity_TX,
  input  StartTX,
  input  TestSer,
  input  TestSerEn,
  input  Stopbit_TX,
  output Serial,
  output [3:0] Display,
  output Parity_RX,
  output Stopbit
);

  wire D0, D1, D2, D3, d_ff_1_q, d_ff_2_q, d_ff_3_q, d_ff_4_q, d_ff_5_q, d_ff_6_q, d_ff_7_q, d_ff_8_q,
       d_ff_9_q, d_ff_10_q, d_ff_11_q, d_ff_12_q, d_ff_13_q, DataReady, multiplexer_1_out, multiplexer_2_out,
       multiplexer_3_out, multiplexer_4_out, multiplexer_5_out, multiplexer_6_out, multiplexer_7_out,
       not_1_out, not_2_out, Parity_RX_t, priorityencoder_1_any, Q0, Q1, Q2, Q3, Stopbit_RX;
  wire [3:0] priorityencoder_1_num;

  not not_1 (not_1_out, StartTX);
  Multiplexer multiplexer_1 (.sel(CLK), .in_0(StartTX), .in_1(not_1_out), .out(multiplexer_1_out));
  D_FF d_ff_1 (.D(multiplexer_1_out), .C(CLK), .Q(d_ff_1_q));  // open: nQ
  Multiplexer multiplexer_2 (.sel(CLK), .in_0(d_ff_1_q), .in_1(D0), .out(multiplexer_2_out));
  D_FF d_ff_2 (.D(multiplexer_2_out), .C(CLK), .Q(d_ff_2_q));  // open: nQ
  Multiplexer multiplexer_3 (.sel(CLK), .in_0(d_ff_2_q), .in_1(D1), .out(multiplexer_3_out));
  D_FF d_ff_3 (.D(multiplexer_3_out), .C(CLK), .Q(d_ff_3_q));  // open: nQ
  Multiplexer multiplexer_4 (.sel(CLK), .in_0(d_ff_3_q), .in_1(D2), .out(multiplexer_4_out));
  D_FF d_ff_4 (.D(multiplexer_4_out), .C(CLK), .Q(d_ff_4_q));  // open: nQ
  Multiplexer multiplexer_5 (.sel(CLK), .in_0(d_ff_4_q), .in_1(D3), .out(multiplexer_5_out));
  D_FF d_ff_5 (.D(multiplexer_5_out), .C(CLK), .Q(d_ff_5_q));  // open: nQ
  Multiplexer multiplexer_6 (.sel(CLK), .in_0(d_ff_5_q), .in_1(Parity_TX), .out(multiplexer_6_out));
  D_FF d_ff_6 (.D(multiplexer_6_out), .C(CLK), .Q(d_ff_6_q));  // open: nQ
  Multiplexer multiplexer_7 (.sel(CLK), .in_0(d_ff_6_q), .in_1(Stopbit_TX), .out(multiplexer_7_out));
  D_FF d_ff_7 (.D(multiplexer_7_out), .C(CLK), .Q(d_ff_7_q));  // open: nQ
  assign Serial = StartTX ? d_ff_7_q : 1'bz;  // Driver driver_1
  PullUp pullup_1 (.out(Serial));
  Seven_Seg_Hex seven_seg_hex_1 (.d(priorityencoder_1_num), .dp(1'b0));
  PriorityEncoder #(.Selector_Bits(4)) priorityencoder_1 (
    .in0(B0), .in1(B1), .in2(B2), .in3(B3), .in4(B4), .in5(B5), .in6(B6), .in7(B7), .in8(B8), .in9(B9),
    .in10(1'b0), .in11(1'b0), .in12(1'b0), .in13(1'b0), .in14(1'b0), .in15(1'b0),
    .num(priorityencoder_1_num), .any(priorityencoder_1_any));
  not not_2 (not_2_out, priorityencoder_1_any);
  or or_1 (D3, not_2_out, priorityencoder_1_num[3]);
  D_FF d_ff_8 (.D(Serial), .C(CLK), .Q(d_ff_8_q));  // open: nQ
  or or_2 (D2, not_2_out, priorityencoder_1_num[2]);
  Multiplexer multiplexer_8 (.sel(DataReady), .in_0(d_ff_8_q), .in_1(d_ff_8_q), .out(Stopbit_RX));
  or or_3 (D1, not_2_out, priorityencoder_1_num[1]);
  D_FF d_ff_9 (.D(d_ff_8_q), .C(CLK), .Q(d_ff_9_q));  // open: nQ
  or or_4 (D0, not_2_out, priorityencoder_1_num[0]);
  Multiplexer multiplexer_9 (.sel(DataReady), .in_0(d_ff_9_q), .in_1(d_ff_9_q), .out(Parity_RX_t));
  D_FF d_ff_10 (.D(d_ff_9_q), .C(CLK), .Q(d_ff_10_q));  // open: nQ
  Multiplexer multiplexer_10 (.sel(DataReady), .in_0(d_ff_10_q), .in_1(d_ff_10_q), .out(Q3));
  D_FF d_ff_11 (.D(d_ff_10_q), .C(CLK), .Q(d_ff_11_q));  // open: nQ
  // ScopeTrigger scopetrigger_1: pin names not known; wires that end beside it: CLK
  Multiplexer multiplexer_11 (.sel(DataReady), .in_0(d_ff_11_q), .in_1(d_ff_11_q), .out(Q2));
  assign Serial = TestSerEn ? TestSer : 1'bz;  // Driver driver_2
  D_FF d_ff_12 (.D(d_ff_11_q), .C(CLK), .Q(d_ff_12_q));  // open: nQ
  Multiplexer multiplexer_12 (.sel(DataReady), .in_0(d_ff_12_q), .in_1(d_ff_12_q), .out(Q1));
  D_FF d_ff_13 (.D(d_ff_12_q), .C(CLK), .Q(d_ff_13_q));  // open: nQ
  Multiplexer multiplexer_13 (.sel(DataReady), .in_0(d_ff_13_q), .in_1(d_ff_13_q), .out(Q0));
  D_FF #(.Bits(6)) Display_Register (
    .D({Stopbit_RX, Parity_RX_t, Q3, Q2, Q1, Q0}), .C(DataReady), .Q({Stopbit, Parity_RX, Display}));  // open: nQ
  D_FF d_ff_14 (.D(d_ff_13_q), .C(CLK), .Q(DataReady));  // open: nQ
  Multiplexer multiplexer_14 (.sel(DataReady), .in_0(DataReady), .in_1(DataReady));  // open: out
  Seven_Seg_Hex seven_seg_hex_2 (.d(Display), .dp(1'b0));
  LED led_1 (.in(Parity_RX));
  LED led_2 (.in(Stopbit));

  // Notes on the sheet:
  //   Stopbit_TX: default 1
  //   Do not change anything or connect directly in this block
  //   Modify this to let your transmitter control the buffer
  //   'Buttons' for automated testing (remember StrarTX)
  //   Remove grounds when developing the receiver
  //   Receiver
  //   Transmitter test display
  //   7-bit Counter
  //   You must connect to and use these using tunnels
  //   Data to be transm'd
  //   Parity even or (not) odd
  //   Stopbit
  //   Start TX
  //   System CLK
  //   Serial line
  //   Received data and DataReady
  //   Receiver output display
endmodule

/* Test case Q1-Transmitter:
CLK	Parity_TX StartTX	B0	B1	B2	B3	B4	B5	B6	B7	B8	B9	Serial
0		0	0	0	0	0	0	0	0	0	0	0	0	X
C		0	0	0	0	0	0	0	0	0	0	0	0	1
C		0	0	0	0	0	0	0	0	0	0	0	0	1
C		0	0	0	0	0	0	0	0	0	0	0	0	1 
C		0	0	0	0	0	0	0	1	0	0	0	0	1 # set B5 to one
C		0	0	0	0	0	0	0	1	0	0	0	0	1 #start transmission
C		0	1	0	0	0	0	0	1	0	0	0	0	0 # start bit
C		0	1	0	0	0	0	0	0	0	0	0	0	1 # D0
C		0	1	0	0	0	0	0	0	0	0	0	0	0 # D1
C		0	0	0	0	0	0	0	0	0	0	0	0	1 # D2
C		0	0	0	0	0	0	0	0	0	0	0	0	0 # D3
C		0	0	0	0	0	0	0	0	0	0	0	0	0 # parity bit
C		0	0	0	0	0	0	0	0	0	0	0	0	1 # stop bit
C		0	0	0	0	0	0	0	0	0	0	0	0	1 
C		0	0	0	0	0	0	0	0	0	0	0	0	1
C		0	0	0	0	0	0	0	0	0	0	0	0	1
C		0	0	0	0	0	0	0	0	0	0	0	0	1
C		1	0	0	0	0	0	0	0	0	0	0	0	1 # odd parity
C		1	0	0	0	0	0	0	0	0	0	0	1	1 # set B9 to one
C		1	0	0	0	0	0	0	0	0	0	0	1	1 #start transmission
C		1	1	0	0	0	0	0	0	0	0	0	1	0 # start bit
C		1	1	0	0	0	0	0	0	0	0	0	0	1 # D0
C		1	1	0	0	0	0	0	0	0	0	0	0	0 # D1
C		1	0	0	0	0	0	0	0	0	0	0	0	0 # D2
C		1	0	0	0	0	0	0	0	0	0	0	0	1 # D3
C		1	0	0	0	0	0	0	0	0	0	0	0	1 # parity bit
C		1	0	0	0	0	0	0	0	0	0	0	0	1 # stop bit
C		1	0	0	0	0	0	0	0	0	0	0	0	1 
C		1	0	0	0	0	0	0	0	0	0	0	0	1
C		0	0	0	0	0	0	0	0	0	0	0	0	1
C		0	0	0	0	0	0	0	0	0	0	0	0	1
C		0	0	0	0	0	0	0	0	0	0	0	0	1
*/

/* Test case Q2-Receiver:
CLK	TestSerEn	TestSer	Display	
0	1	1	X	
C	1	1	X	
C	1	1	X	
C	1	1	X	
C	1	1	X	
C	1	1	X	
C	1	0	X	# start bit
C	1	1	X	#d0
C	1	0	X	#d1
C	1	1	X	#d2
C	1	0	X	#d3
C	1	0	X	#partiy
C	1	1	5	#stopbit
C	1	1	5	
C	1	1	5	
C	1	1	5	
C	1	1	5	
C	1	1	X	
C	1	0	X	# start bit
C	1	1	X	#d0
C	1	1	X	#d1
C	1	1	X	#d2
C	1	0	X	#d3
C	1	1	X	#partiy
C	1	1	7	#stopbit
C	1	1	7	
C	1	1	7	
C	1	1	7	
C	1	1	7	
*/

/* Test case Q3System:
CLK	Parity_TX	StartTX	B0	B1	B2	B3	B4	B5	B6	B7	B8	B9	Display	Parity_RX
0	0	0	0	0	0	0	0	0	0	0	0	0	X	0
C	0	0	0	0	0	0	0	0	0	0	0	0	X	0
C	0	0	0	0	0	0	0	0	0	0	0	0	X	0
C	0	0	0	0	0	0	0	0	0	0	0	0	X	0
C	0	0	0	0	0	0	0	1	0	0	0	0	X	0
C	0	0	0	0	0	0	0	1	0	0	0	0	X	0
C	0	1	0	0	0	0	0	1	0	0	0	0	X	0
C	0	1	0	0	0	0	0	0	0	0	0	0	X	0
C	0	1	0	0	0	0	0	0	0	0	0	0	X	0
C	0	0	0	0	0	0	0	0	0	0	0	0	X	0
C	0	0	0	0	0	0	0	0	0	0	0	0	X	0
C	0	0	0	0	0	0	0	0	0	0	0	0	X	0
C	0	0	0	0	0	0	0	0	0	0	0	0	X	0
C	0	0	0	0	0	0	0	0	0	0	0	0	X	0
C	0	0	0	0	0	0	0	0	0	0	0	0	5	0
C	0	0	0	0	0	0	0	0	0	0	0	0	5	0
C	0	0	0	0	0	0	0	0	0	0	0	0	5	0
C	1	0	0	0	0	0	0	0	0	0	0	0	5	0
C	1	0	0	0	0	0	0	0	0	0	0	1	5	0
C	1	0	0	0	0	0	0	0	0	0	0	1	5	0
C	1	1	0	0	0	0	0	0	0	0	0	1	5	0
C	1	1	0	0	0	0	0	0	0	0	0	0	5	0
C	1	1	0	0	0	0	0	0	0	0	0	0	5	0
C	1	0	0	0	0	0	0	0	0	0	0	0	5	0
C	1	0	0	0	0	0	0	0	0	0	0	0	5	0
C	1	0	0	0	0	0	0	0	0	0	0	0	5	0
C	1	0	0	0	0	0	0	0	0	0	0	0	5	0
C	1	0	0	0	0	0	0	0	0	0	0	0	9	1
C	1	0	0	0	0	0	0	0	0	0	0	0	9	1
C	0	0	0	0	0	0	0	0	0	0	0	0	9	1
C	0	0	0	0	0	0	0	0	0	0	0	0	9	1
C	0	0	0	0	0	0	0	0	0	0	0	0	9	1
C	0	0	0	0	0	1	0	0	0	0	0	0	9	1
C	0	0	0	0	0	1	0	0	0	0	0	0	9	1
C	0	1	0	0	0	1	0	0	0	0	0	0	9	1
C	0	1	0	0	0	0	0	0	0	0	0	0	9	1
C	0	1	0	0	0	0	0	0	0	0	0	0	9	1
C	0	1	0	0	0	0	0	0	0	0	0	0	9	1
C	0	1	0	0	0	0	0	0	0	0	0	0	9	1
C	0	1	0	0	0	0	0	0	0	0	0	0	9	1
C	0	1	0	0	0	0	0	0	0	0	0	0	9	1
C	0	1	0	0	0	0	0	0	0	0	0	0	3	0
C	0	1	0	0	0	0	0	0	0	0	0	0	3	0
C	0	1	0	0	0	0	0	0	0	0	0	0	3	0
C	0	1	0	0	0	0	0	0	0	0	0	0	3	0
C	0	1	0	0	0	0	0	0	0	0	0	0	3	0
*/
